// Logisim project RGAndALU.circ as structural Verilog: 6 circuits, main circuit AU
module AU (
  input  in_1,
  input  [7:0] in_2,
  input  [7:0] in_3,
  output [7:0] out_4
);

  wire [7:0] adder_1_out, multiplexer_1_out, not_1_out;

  assign not_1_out = ~in_3;  // NOT_Gate not_1, 8 bits wide
  Adder adder_1 (.a(not_1_out), .b(8'h1), .out(adder_1_out));  // open: cin, cout
  Multiplexer #(.width(8)) multiplexer_1 (
    .in0(adder_1_out), .in1(in_3), .out(multiplexer_1_out), .sel(in_1));  // open: en
  Adder adder_2 (.a(in_2), .b(multiplexer_1_out), .out(out_4));  // open: cin, cout
endmodule

module LU (
  input  in_1,
  input  [7:0] in_2,
  input  [7:0] in_3,
  output [7:0] out_4
);

  wire [7:0] and_1_out, or_1_out;

  assign and_1_out = in_2 & in_3;  // AND_Gate and_1, 8 bits wide
  assign or_1_out = in_2 | in_3;  // OR_Gate or_1, 8 bits wide
  Multiplexer #(.width(8)) multiplexer_1 (.in0(or_1_out), .in1(and_1_out), .out(out_4), .sel(in_1));  // open: en
endmodule

module ALU (
  input  [3:0] in_1,
  input  [7:0] in_2,
  input  [7:0] in_3,
  output [7:0] out_4
);

  wire [7:0] au_1_out_4, lu_1_out_4;

  AU au_1 (.in_1(in_1[1]), .in_2(in_2), .in_3(in_3), .out_4(au_1_out_4));
  LU lu_1 (.in_1(in_1[0]), .in_2(in_2), .in_3(in_3), .out_4(lu_1_out_4));
  Multiplexer #(.width(8)) multiplexer_1 (.in0(lu_1_out_4), .in1(au_1_out_4), .out(out_4), .sel(in_1[2]));  // open: en
endmodule

module RegisterGroup (
  input  [4:0] in_1,
  input  [7:0] in_2,
  input  [4:0] in_3,
  input  in_4,
  input  in_5,
  output [7:0] out_6
);

  wire and_1_out, and_2_out, and_3_out, and_4_out, and_5_out, and_6_out, and_7_out, decoder_1_out0,
       decoder_1_out1, decoder_1_out2, decoder_1_out3, decoder_1_out4, decoder_1_out5, decoder_1_out6,
       decoder_1_out7;
  wire [7:0] register_1_q, register_2_q, register_3_q, register_4_q, register_5_q, register_6_q,
       register_7_q, register_8_q;

  Decoder #(.select(3)) decoder_1 (
    .out0(decoder_1_out0), .out1(decoder_1_out1), .out2(decoder_1_out2), .out3(decoder_1_out3),
    .out4(decoder_1_out4), .out5(decoder_1_out5), .out6(decoder_1_out6), .out7(decoder_1_out7),
    .sel(in_3[2:0]));  // open: en
  and and_1 (and_1_out, decoder_1_out0, in_4);
  and and_2 (and_2_out, decoder_1_out1, in_4);
  and and_3 (and_3_out, decoder_1_out2, in_4);
  and and_4 (and_4_out, decoder_1_out3, in_4);
  and and_5 (and_5_out, decoder_1_out4, in_4);
  and and_6 (and_6_out, decoder_1_out5, in_4);
  and and_7 (and_7_out, decoder_1_out6, in_4);
  // AND_Gate and_8 has open pins: in0=decoder_1_out7, in1=in_4, out=open
  Register register_1 (.D(in_2), .en(and_1_out), .Q(register_1_q), .clk(in_5));  // open: clr
  Register register_2 (.D(in_2), .en(and_2_out), .Q(register_2_q), .clk(in_5));  // open: clr
  Register register_3 (.D(in_2), .en(and_3_out), .Q(register_3_q), .clk(in_5));  // open: clr
  Register register_4 (.D(in_2), .en(and_4_out), .Q(register_4_q), .clk(in_5));  // open: clr
  Register register_5 (.D(in_2), .en(and_5_out), .Q(register_5_q), .clk(in_5));  // open: clr
  Register register_6 (.D(in_2), .en(and_6_out), .Q(register_6_q), .clk(in_5));  // open: clr
  Register register_7 (.D(in_2), .en(and_7_out), .Q(register_7_q), .clk(in_5));  // open: clr
  Register register_8 (.Q(register_8_q), .clr(1'b1));  // open: D, en, clk
  Multiplexer #(.select(3), .width(8)) multiplexer_1 (
    .in0(register_1_q), .in1(register_2_q), .in2(register_3_q), .in3(register_4_q), .in4(register_5_q),
    .in5(register_6_q), .in6(register_7_q), .in7(register_8_q), .out(out_6), .sel(in_1[2:0]));  // open: en
endmodule

module test (
  output [7:0] out_1,
  output [7:0] out_2
);

  wire clock_1_out, not_1_out;

  not not_1 (not_1_out, 1'b0);
  Clock clock_1 (.out(clock_1_out));
  ROM rom_1 (.addr(8'h1), .data(out_1));  // open: sel
  RAM #(.bus("separate")) ram_1 (
    .addr(8'h1), .din(8'h4), .data(out_2), .str(1'b0), .clk(clock_1_out), .ld(not_1_out));  // open: sel, clr
endmodule

module RGAndALU (
);

  wire clock_1_out, clock_2_out, not_1_out;
  wire [3:0] bit_extender_2_out;
  wire [7:0] alu_1_out_4, bit_extender_1_out, multiplexer_1_out, ram_1_data, registergroup_1_out_6, undriven;

  Clock clock_1 (.out(clock_1_out));
  Bit_Extender #(.in_width(10), .out_width(8)) bit_extender_1 (.in(10'h4), .out(bit_extender_1_out));
  Bit_Extender #(.in_width(6), .out_width(4)) bit_extender_2 (.in(6'b000110), .out(bit_extender_2_out));
  RegisterGroup registergroup_1 (
    .in_1(5'b00111), .in_2(multiplexer_1_out), .in_3({5{1'b0}}), .in_4(1'b1), .out_6(registergroup_1_out_6),
    .in_5(clock_1_out));
  Multiplexer #(.width(8)) multiplexer_1 (
    .in0(alu_1_out_4), .in1(ram_1_data), .out(multiplexer_1_out), .sel(1'b0));  // open: en
  ALU alu_1 (.in_1(bit_extender_2_out), .in_2(registergroup_1_out_6), .in_3(bit_extender_1_out), .out_4(alu_1_out_4));
  not not_1 (not_1_out, 1'b0);
  RAM #(.bus("separate")) ram_1 (
    .addr(undriven), .din(registergroup_1_out_6), .data(ram_1_data), .str(1'b0), .clk(clock_2_out),
    .ld(not_1_out));  // open: sel, clr
  Clock clock_2 (.out(clock_2_out));
endmodule
