// Logisim project 第10-11话.circ as structural Verilog: 14 circuits, main circuit AU
module AU (
  input  in_1,
  input  [7:0] in_2,
  input  [7:0] in_3,
  output [7:0] out_4
);

  wire [7:0] adder_1_out, multiplexer_1_out, not_1_out;

  assign not_1_out = ~in_3;  // NOT_Gate not_1, 8 bits wide
  Adder adder_1 (.a(not_1_out), .b(8'h1), .out(adder_1_out));  // open: cin, cout
  Multiplexer #(.width(8)) multiplexer_1 (
    .in0(adder_1_out), .in1(in_3), .out(multiplexer_1_out), .sel(in_1));  // open: en
  Adder adder_2 (.a(in_2), .b(multiplexer_1_out), .out(out_4));  // open: cin, cout
endmodule

module LU (
  input  in_1,
  input  [7:0] in_2,
  input  [7:0] in_3,
  output [7:0] out_4
);

  wire [7:0] and_1_out, or_1_out;

  assign and_1_out = in_2 & in_3;  // AND_Gate and_1, 8 bits wide
  assign or_1_out = in_2 | in_3;  // OR_Gate or_1, 8 bits wide
  Multiplexer #(.width(8)) multiplexer_1 (.in0(or_1_out), .in1(and_1_out), .out(out_4), .sel(in_1));  // open: en
endmodule

module ALU (
  input  [3:0] in_1,
  input  [7:0] in_2,
  input  [7:0] in_3,
  output [7:0] out_4
);

  wire [7:0] au_1_out_4, lu_1_out_4;

  AU au_1 (.in_1(in_1[1]), .in_2(in_2), .in_3(in_3), .out_4(au_1_out_4));
  LU lu_1 (.in_1(in_1[0]), .in_2(in_2), .in_3(in_3), .out_4(lu_1_out_4));
  Multiplexer #(.width(8)) multiplexer_1 (.in0(lu_1_out_4), .in1(au_1_out_4), .out(out_4), .sel(in_1[2]));  // open: en
endmodule

module RegisterGroup (
  input  [4:0] in_1,
  input  [7:0] in_2,
  input  [4:0] in_3,
  input  in_4,
  input  in_5,
  output [7:0] out_6
);

  wire and_1_out, and_2_out, and_3_out, and_4_out, and_5_out, and_6_out, and_7_out, decoder_1_out0,
       decoder_1_out1, decoder_1_out2, decoder_1_out3, decoder_1_out4, decoder_1_out5, decoder_1_out6,
       decoder_1_out7;
  wire [7:0] register_1_q, register_2_q, register_3_q, register_4_q, register_5_q, register_6_q,
       register_7_q, register_8_q;

  Decoder #(.select(3)) decoder_1 (
    .out0(decoder_1_out0), .out1(decoder_1_out1), .out2(decoder_1_out2), .out3(decoder_1_out3),
    .out4(decoder_1_out4), .out5(decoder_1_out5), .out6(decoder_1_out6), .out7(decoder_1_out7),
    .sel(in_3[2:0]));  // open: en
  and and_1 (and_1_out, decoder_1_out0, in_4);
  and and_2 (and_2_out, decoder_1_out1, in_4);
  and and_3 (and_3_out, decoder_1_out2, in_4);
  and and_4 (and_4_out, decoder_1_out3, in_4);
  and and_5 (and_5_out, decoder_1_out4, in_4);
  and and_6 (and_6_out, decoder_1_out5, in_4);
  and and_7 (and_7_out, decoder_1_out6, in_4);
  // AND_Gate and_8 has open pins: in0=decoder_1_out7, in1=in_4, out=open
  Register register_1 (.D(in_2), .en(and_1_out), .Q(register_1_q), .clk(in_5));  // open: clr
  Register register_2 (.D(in_2), .en(and_2_out), .Q(register_2_q), .clk(in_5));  // open: clr
  Register register_3 (.D(in_2), .en(and_3_out), .Q(register_3_q), .clk(in_5));  // open: clr
  Register register_4 (.D(in_2), .en(and_4_out), .Q(register_4_q), .clk(in_5));  // open: clr
  Register register_5 (.D(in_2), .en(and_5_out), .Q(register_5_q), .clk(in_5));  // open: clr
  Register register_6 (.D(in_2), .en(and_6_out), .Q(register_6_q), .clk(in_5));  // open: clr
  Register register_7 (.D(in_2), .en(and_7_out), .Q(register_7_q), .clk(in_5));  // open: clr
  Register register_8 (.Q(register_8_q), .clr(1'b1));  // open: D, en, clk
  Multiplexer #(.select(3), .width(8)) multiplexer_1 (
    .in0(register_1_q), .in1(register_2_q), .in2(register_3_q), .in3(register_4_q), .in4(register_5_q),
    .in5(register_6_q), .in6(register_7_q), .in7(register_8_q), .out(out_6), .sel(in_1[2:0]));  // open: en
endmodule

module RegisterGroupV2 (
  input  [4:0] in_1,
  input  [4:0] in_2,
  input  [7:0] in_3,
  input  [4:0] in_4,
  input  in_5,
  input  in_6,
  output [7:0] out_7,
  output [7:0] out_8
);

  wire and_1_out, and_2_out, and_3_out, and_4_out, and_5_out, and_6_out, and_7_out, decoder_1_out0,
       decoder_1_out1, decoder_1_out2, decoder_1_out3, decoder_1_out4, decoder_1_out5, decoder_1_out6,
       decoder_1_out7;
  wire [2:0] bit_extender_1_out, bit_extender_2_out, bit_extender_3_out;
  wire [7:0] register_1_q, register_2_q, register_3_q, register_4_q, register_5_q, register_6_q,
       register_7_q, register_8_q;

  Bit_Extender #(.in_width(5), .out_width(3)) bit_extender_1 (.in(in_1), .out(bit_extender_1_out));
  Bit_Extender #(.in_width(5), .out_width(3)) bit_extender_2 (.in(in_2), .out(bit_extender_2_out));
  Decoder #(.select(3)) decoder_1 (
    .out0(decoder_1_out0), .out1(decoder_1_out1), .out2(decoder_1_out2), .out3(decoder_1_out3),
    .out4(decoder_1_out4), .out5(decoder_1_out5), .out6(decoder_1_out6), .out7(decoder_1_out7),
    .sel(bit_extender_3_out));  // open: en
  Bit_Extender #(.in_width(5), .out_width(3)) bit_extender_3 (.in(in_4), .out(bit_extender_3_out));
  and and_1 (and_1_out, decoder_1_out0, in_5);
  and and_2 (and_2_out, decoder_1_out1, in_5);
  and and_3 (and_3_out, decoder_1_out2, in_5);
  and and_4 (and_4_out, decoder_1_out3, in_5);
  and and_5 (and_5_out, decoder_1_out4, in_5);
  and and_6 (and_6_out, decoder_1_out5, in_5);
  and and_7 (and_7_out, decoder_1_out6, in_5);
  // AND_Gate and_8 has open pins: in0=decoder_1_out7, in1=in_5, out=open
  Register register_1 (.D(in_3), .en(and_1_out), .Q(register_1_q), .clk(in_6));  // open: clr
  Register register_2 (.D(in_3), .en(and_2_out), .Q(register_2_q), .clk(in_6));  // open: clr
  Register register_3 (.D(in_3), .en(and_3_out), .Q(register_3_q), .clk(in_6));  // open: clr
  Register register_4 (.D(in_3), .en(and_4_out), .Q(register_4_q), .clk(in_6));  // open: clr
  Register register_5 (.D(in_3), .en(and_5_out), .Q(register_5_q), .clk(in_6));  // open: clr
  Register register_6 (.D(in_3), .en(and_6_out), .Q(register_6_q), .clk(in_6));  // open: clr
  Register register_7 (.D(in_3), .en(and_7_out), .Q(register_7_q), .clk(in_6));  // open: clr
  Register register_8 (.Q(register_8_q), .clr(1'b1));  // open: D, en, clk
  Multiplexer #(.select(3), .width(8)) multiplexer_1 (
    .in0(register_1_q), .in1(register_2_q), .in2(register_3_q), .in3(register_4_q), .in4(register_5_q),
    .in5(register_6_q), .in6(register_7_q), .in7(register_8_q), .out(out_7), .sel(bit_extender_1_out));  // open: en
  Multiplexer #(.select(3), .width(8)) multiplexer_2 (
    .in0(register_1_q), .in1(register_2_q), .in2(register_3_q), .in3(register_4_q), .in4(register_5_q),
    .in5(register_6_q), .in6(register_7_q), .in7(register_8_q), .out(out_8), .sel(bit_extender_2_out));  // open: en
endmodule

module RegisterGroupV3 (
  input  [4:0] in_1,
  input  [4:0] in_2,
  input  [7:0] in_3,
  input  [4:0] in_4,
  input  in_5,
  input  in_6,
  output [7:0] out_7,
  output [7:0] out_8,
  output [7:0] out_9,
  output [7:0] out_10,
  output [7:0] out_11
);

  wire and_1_out, and_2_out, and_3_out, and_4_out, and_5_out, and_6_out, and_7_out, decoder_1_out0,
       decoder_1_out1, decoder_1_out2, decoder_1_out3, decoder_1_out4, decoder_1_out5, decoder_1_out6,
       decoder_1_out7;
  wire [2:0] bit_extender_1_out, bit_extender_2_out, bit_extender_3_out;
  wire [7:0] register_1_q, register_2_q, register_3_q, register_4_q, register_8_q;

  Bit_Extender #(.in_width(5), .out_width(3)) bit_extender_1 (.in(in_1), .out(bit_extender_1_out));
  Bit_Extender #(.in_width(5), .out_width(3)) bit_extender_2 (.in(in_2), .out(bit_extender_2_out));
  Decoder #(.select(3)) decoder_1 (
    .out0(decoder_1_out0), .out1(decoder_1_out1), .out2(decoder_1_out2), .out3(decoder_1_out3),
    .out4(decoder_1_out4), .out5(decoder_1_out5), .out6(decoder_1_out6), .out7(decoder_1_out7),
    .sel(bit_extender_3_out));  // open: en
  Bit_Extender #(.in_width(5), .out_width(3)) bit_extender_3 (.in(in_4), .out(bit_extender_3_out));
  and and_1 (and_1_out, decoder_1_out0, in_5);
  and and_2 (and_2_out, decoder_1_out1, in_5);
  and and_3 (and_3_out, decoder_1_out2, in_5);
  and and_4 (and_4_out, decoder_1_out3, in_5);
  and and_5 (and_5_out, decoder_1_out4, in_5);
  and and_6 (and_6_out, decoder_1_out5, in_5);
  and and_7 (and_7_out, decoder_1_out6, in_5);
  // AND_Gate and_8 has open pins: in0=decoder_1_out7, in1=in_5, out=open
  Register register_1 (.D(in_3), .en(and_1_out), .Q(register_1_q), .clk(in_6));  // open: clr
  Register register_2 (.D(in_3), .en(and_2_out), .Q(register_2_q), .clk(in_6));  // open: clr
  Register register_3 (.D(in_3), .en(and_3_out), .Q(register_3_q), .clk(in_6));  // open: clr
  Register register_4 (.D(in_3), .en(and_4_out), .Q(register_4_q), .clk(in_6));  // open: clr
  Register register_5 (.D(in_3), .en(and_5_out), .Q(out_9), .clk(in_6));  // open: clr
  Register register_6 (.D(in_3), .en(and_6_out), .Q(out_10), .clk(in_6));  // open: clr
  Register register_7 (.D(in_3), .en(and_7_out), .Q(out_11), .clk(in_6));  // open: clr
  Register register_8 (.Q(register_8_q), .clr(1'b1));  // open: D, en, clk
  Multiplexer #(.select(3), .width(8)) multiplexer_1 (
    .in0(register_1_q), .in1(register_2_q), .in2(register_3_q), .in3(register_4_q), .in4(out_9),
    .in5(out_10), .in6(out_11), .in7(register_8_q), .out(out_7), .sel(bit_extender_1_out));  // open: en
  Multiplexer #(.select(3), .width(8)) multiplexer_2 (
    .in0(register_1_q), .in1(register_2_q), .in2(register_3_q), .in3(register_4_q), .in4(out_9),
    .in5(out_10), .in6(out_11), .in7(register_8_q), .out(out_8), .sel(bit_extender_2_out));  // open: en
endmodule

module test (
  output [7:0] out_1,
  output [7:0] out_2
);

  wire clock_1_out, not_1_out;

  not not_1 (not_1_out, 1'b0);
  Clock clock_1 (.out(clock_1_out));
  ROM rom_1 (.addr(8'h1), .data(out_1));  // open: sel
  RAM #(.bus("separate")) ram_1 (
    .addr(8'h1), .din(8'h4), .data(out_2), .str(1'b0), .clk(clock_1_out), .ld(not_1_out));  // open: sel, clr
endmodule

module RGAndALU (
);

  wire clock_1_out, clock_2_out, not_1_out;
  wire [3:0] bit_extender_2_out;
  wire [7:0] alu_1_out_4, bit_extender_1_out, multiplexer_1_out, ram_1_data, registergroup_1_out_6, undriven;

  Clock clock_1 (.out(clock_1_out));
  Bit_Extender #(.in_width(10), .out_width(8)) bit_extender_1 (.in(10'h1), .out(bit_extender_1_out));
  Bit_Extender #(.in_width(6), .out_width(4)) bit_extender_2 (.in(6'b000100), .out(bit_extender_2_out));
  RegisterGroup registergroup_1 (
    .in_1({5{1'b0}}), .in_2(multiplexer_1_out), .in_3(5'b00001), .in_4(1'b1), .out_6(registergroup_1_out_6),
    .in_5(clock_1_out));
  Multiplexer #(.width(8)) multiplexer_1 (
    .in0(alu_1_out_4), .in1(ram_1_data), .out(multiplexer_1_out), .sel(1'b0));  // open: en
  ALU alu_1 (.in_1(bit_extender_2_out), .in_2(registergroup_1_out_6), .in_3(bit_extender_1_out), .out_4(alu_1_out_4));
  not not_1 (not_1_out, 1'b0);
  RAM #(.bus("separate")) ram_1 (
    .addr(undriven), .din(registergroup_1_out_6), .data(ram_1_data), .str(1'b0), .clk(clock_2_out),
    .ld(not_1_out));  // open: sel, clr
  Clock clock_2 (.out(clock_2_out));
endmodule

module CPU (
  input  [7:0] DRAMOut,
  input  [31:0] Ins,
  input  CLK,
  output [7:0] out_4,
  output W_R_prime,
  output [7:0] RAMAddr,
  output [7:0] RAMIn,
  output [7:0] P0,
  output [7:0] P1,
  output [7:0] P2
);

  wire [3:0] bit_extender_3_out;
  wire [7:0] bit_extender_1_out, bit_extender_2_out, multiplexer_1_out, registergroupv3_1_out_7;

  Bit_Extender #(.in_width(26), .out_width(8)) bit_extender_1 (.in(Ins[25:0]), .out(bit_extender_1_out));
  RegisterGroupV3 registergroupv3_1 (
    .in_1(Ins[25:21]), .in_2(Ins[20:16]), .in_3(multiplexer_1_out), .in_4(Ins[20:16]), .in_5(Ins[31]),
    .in_6(CLK), .out_7(registergroupv3_1_out_7), .out_8(RAMIn), .out_9(P0), .out_10(P1), .out_11(P2));
  Bit_Extender #(.in_width(10), .out_width(8)) bit_extender_2 (.in(Ins[15:6]), .out(bit_extender_2_out));
  Bit_Extender #(.in_width(6), .out_width(4)) bit_extender_3 (.in(Ins[5:0]), .out(bit_extender_3_out));
  PC pc_1 (.CLK(CLK), .out_4(out_4), .Jump(Ins[28]), .JumpPos(bit_extender_1_out));
  Multiplexer #(.width(8)) multiplexer_1 (
    .in0(RAMAddr), .in1(DRAMOut), .out(multiplexer_1_out), .sel(Ins[30]));  // open: en
  ALU alu_1 (.in_1(bit_extender_3_out), .in_2(registergroupv3_1_out_7), .in_3(bit_extender_2_out), .out_4(RAMAddr));

  assign W_R_prime = Ins[29];
endmodule

module Motherboard (
);

  wire clock_1_out, cpu_1_w_r_prime, not_1_out;
  wire [7:0] cpu_1_out_4, cpu_1_p0, cpu_1_p1, cpu_1_p2, cpu_1_ramaddr, cpu_1_ramin, ram_1_data,
       screendecoder_1_out_6, screendecoder_1_out_7, screendecoder_1_out_8, screendecoder_1_out_9,
       screendecoder_1_out_10, screendecoder_1_out_11, screendecoder_1_out_12, screendecoder_1_out_13;
  wire [31:0] rom_1_data;

  ROM #(.dataWidth(32)) rom_1 (.addr(cpu_1_out_4), .data(rom_1_data));  // open: sel
  Clock clock_1 (.out(clock_1_out));
  CPU cpu_1 (
    .Ins(rom_1_data), .W_R_prime(cpu_1_w_r_prime), .RAMIn(cpu_1_ramin), .RAMAddr(cpu_1_ramaddr),
    .CLK(clock_1_out), .DRAMOut(ram_1_data), .out_4(cpu_1_out_4), .P0(cpu_1_p0), .P1(cpu_1_p1), .P2(cpu_1_p2));
  ScreenDecoder screendecoder_1 (
    .Cols(cpu_1_p1), .Rows(cpu_1_p0), .CLK(cpu_1_p2[2]), .out_6(screendecoder_1_out_6),
    .out_7(screendecoder_1_out_7), .out_8(screendecoder_1_out_8), .out_9(screendecoder_1_out_9),
    .out_10(screendecoder_1_out_10), .out_11(screendecoder_1_out_11), .out_12(screendecoder_1_out_12),
    .out_13(screendecoder_1_out_13), .FLASH(cpu_1_p2[1]), .CLR(cpu_1_p2[0]));
  DotMatrix #(.matrixcols(8), .matrixrows(8)) dotmatrix_1 (
    .col0(screendecoder_1_out_6), .col1(screendecoder_1_out_7), .col2(screendecoder_1_out_8),
    .col3(screendecoder_1_out_9), .col4(screendecoder_1_out_10), .col5(screendecoder_1_out_11),
    .col6(screendecoder_1_out_12), .col7(screendecoder_1_out_13));
  RAM #(.bus("separate")) ram_1 (
    .addr(cpu_1_ramaddr), .din(cpu_1_ramin), .data(ram_1_data), .str(cpu_1_w_r_prime), .clk(clock_1_out),
    .ld(not_1_out));  // open: sel, clr
  not not_1 (not_1_out, cpu_1_w_r_prime);

  // Notes on the sheet:
  //   contents of rom_1 (hex, n*v repeats v):
  //   80e00046 80e10106 20010006 20010046 80e00046 c0040006 c0050046 80e60106 80e60086 c0010006 80210046
  //   20010006 80e60046 80e00046 c0040006 c0050046 80e60106 80e60086 10000009
endmodule

module PC (
  input  [7:0] JumpPos,
  input  Jump,
  input  CLK,
  output [7:0] out_4
);

  wire [7:0] adder_1_out, multiplexer_1_out;

  Register register_1 (.D(multiplexer_1_out), .Q(out_4), .clk(CLK));  // open: en, clr
  Adder adder_1 (.a(out_4), .b(8'h1), .out(adder_1_out));  // open: cin, cout
  Multiplexer #(.width(8)) multiplexer_1 (
    .in0(adder_1_out), .in1(JumpPos), .out(multiplexer_1_out), .sel(Jump));  // open: en
endmodule

module ScreenDecoder (
  input  [7:0] Cols,
  input  [7:0] Rows,
  input  CLK,
  input  FLASH,
  input  CLR,
  output [7:0] out_6,
  output [7:0] out_7,
  output [7:0] out_8,
  output [7:0] out_9,
  output [7:0] out_10,
  output [7:0] out_11,
  output [7:0] out_12,
  output [7:0] out_13
);

  wire demultiplexer_1_out0, demultiplexer_1_out1, demultiplexer_1_out2, demultiplexer_1_out3,
       demultiplexer_1_out4, demultiplexer_1_out5, demultiplexer_1_out6, demultiplexer_1_out7,
       demultiplexer_2_out0, demultiplexer_2_out1, demultiplexer_2_out2, demultiplexer_2_out3,
       demultiplexer_2_out4, demultiplexer_2_out5, demultiplexer_2_out6, demultiplexer_2_out7;
  wire [7:0] register_1_q, register_2_q, register_3_q, register_4_q, register_5_q, register_6_q,
       register_7_q, register_8_q, screenregsdec_1_out_17, screenregsdec_1_out_18, screenregsdec_1_out_19,
       screenregsdec_1_out_20, screenregsdec_1_out_21, screenregsdec_1_out_22, screenregsdec_1_out_23,
       screenregsdec_1_out_24;

  Demultiplexer #(.select(3)) demultiplexer_1 (
    .out0(demultiplexer_1_out0), .out1(demultiplexer_1_out1), .out2(demultiplexer_1_out2),
    .out3(demultiplexer_1_out3), .out4(demultiplexer_1_out4), .out5(demultiplexer_1_out5),
    .out6(demultiplexer_1_out6), .out7(demultiplexer_1_out7), .in(1'b1), .sel(Rows[2:0]));  // open: en
  Demultiplexer #(.select(3)) demultiplexer_2 (
    .out0(demultiplexer_2_out0), .out1(demultiplexer_2_out1), .out2(demultiplexer_2_out2),
    .out3(demultiplexer_2_out3), .out4(demultiplexer_2_out4), .out5(demultiplexer_2_out5),
    .out6(demultiplexer_2_out6), .out7(demultiplexer_2_out7), .in(1'b1), .sel(Cols[2:0]));  // open: en
  ScreenRegsDec screenregsdec_1 (
    .in_9(demultiplexer_1_out0), .in_10(demultiplexer_1_out1), .in_11(demultiplexer_1_out2),
    .in_12(demultiplexer_1_out3), .in_13(demultiplexer_1_out4), .in_14(demultiplexer_1_out5),
    .in_15(demultiplexer_1_out6), .in_16(demultiplexer_1_out7), .out_17(screenregsdec_1_out_17),
    .out_18(screenregsdec_1_out_18), .out_19(screenregsdec_1_out_19), .out_20(screenregsdec_1_out_20),
    .out_21(screenregsdec_1_out_21), .out_22(screenregsdec_1_out_22), .out_23(screenregsdec_1_out_23),
    .out_24(screenregsdec_1_out_24), .in_1(demultiplexer_2_out0), .in_2(demultiplexer_2_out1),
    .in_3(demultiplexer_2_out2), .in_4(demultiplexer_2_out3), .in_5(demultiplexer_2_out4),
    .in_6(demultiplexer_2_out5), .in_7(demultiplexer_2_out6), .in_8(demultiplexer_2_out7));
  Register #(.width(1)) register_1 (
    .D(1'b1), .en(screenregsdec_1_out_17[0]), .Q(register_1_q[0]), .clk(CLK), .clr(CLR));
  Register #(.width(1)) register_2 (
    .D(1'b1), .en(screenregsdec_1_out_18[0]), .Q(register_2_q[0]), .clk(CLK), .clr(CLR));
  Register #(.width(1)) register_3 (
    .D(1'b1), .en(screenregsdec_1_out_19[0]), .Q(register_3_q[0]), .clk(CLK), .clr(CLR));
  Register #(.width(1)) register_4 (
    .D(1'b1), .en(screenregsdec_1_out_20[0]), .Q(register_4_q[0]), .clk(CLK), .clr(CLR));
  Register #(.width(1)) register_5 (
    .D(1'b1), .en(screenregsdec_1_out_21[0]), .Q(register_5_q[0]), .clk(CLK), .clr(CLR));
  Register #(.width(1)) register_6 (
    .D(1'b1), .en(screenregsdec_1_out_22[0]), .Q(register_6_q[0]), .clk(CLK), .clr(CLR));
  Register #(.width(1)) register_7 (
    .D(1'b1), .en(screenregsdec_1_out_23[0]), .Q(register_7_q[0]), .clk(CLK), .clr(CLR));
  Register #(.width(1)) register_8 (
    .D(1'b1), .en(screenregsdec_1_out_24[0]), .Q(register_8_q[0]), .clk(CLK), .clr(CLR));
  Register #(.width(1)) register_9 (
    .D(1'b1), .en(screenregsdec_1_out_17[1]), .Q(register_1_q[1]), .clk(CLK), .clr(CLR));
  Register #(.width(1)) register_10 (
    .D(1'b1), .en(screenregsdec_1_out_18[1]), .Q(register_2_q[1]), .clk(CLK), .clr(CLR));
  Register #(.width(1)) register_11 (
    .D(1'b1), .en(screenregsdec_1_out_19[1]), .Q(register_3_q[1]), .clk(CLK), .clr(CLR));
  Register #(.width(1)) register_12 (
    .D(1'b1), .en(screenregsdec_1_out_20[1]), .Q(register_4_q[1]), .clk(CLK), .clr(CLR));
  Register #(.width(1)) register_13 (
    .D(1'b1), .en(screenregsdec_1_out_21[1]), .Q(register_5_q[1]), .clk(CLK), .clr(CLR));
  Register #(.width(1)) register_14 (
    .D(1'b1), .en(screenregsdec_1_out_22[1]), .Q(register_6_q[1]), .clk(CLK), .clr(CLR));
  Register #(.width(1)) register_15 (
    .D(1'b1), .en(screenregsdec_1_out_23[1]), .Q(register_7_q[1]), .clk(CLK), .clr(CLR));
  Register #(.width(1)) register_16 (
    .D(1'b1), .en(screenregsdec_1_out_24[1]), .Q(register_8_q[1]), .clk(CLK), .clr(CLR));
  Register #(.width(1)) register_17 (
    .D(1'b1), .en(screenregsdec_1_out_17[2]), .Q(register_1_q[2]), .clk(CLK), .clr(CLR));
  Register #(.width(1)) register_18 (
    .D(1'b1), .en(screenregsdec_1_out_18[2]), .Q(register_2_q[2]), .clk(CLK), .clr(CLR));
  Register #(.width(1)) register_19 (
    .D(1'b1), .en(screenregsdec_1_out_19[2]), .Q(register_3_q[2]), .clk(CLK), .clr(CLR));
  Register #(.width(1)) register_20 (
    .D(1'b1), .en(screenregsdec_1_out_20[2]), .Q(register_4_q[2]), .clk(CLK), .clr(CLR));
  Register #(.width(1)) register_21 (
    .D(1'b1), .en(screenregsdec_1_out_21[2]), .Q(register_5_q[2]), .clk(CLK), .clr(CLR));
  Register #(.width(1)) register_22 (
    .D(1'b1), .en(screenregsdec_1_out_22[2]), .Q(register_6_q[2]), .clk(CLK), .clr(CLR));
  Register #(.width(1)) register_23 (
    .D(1'b1), .en(screenregsdec_1_out_23[2]), .Q(register_7_q[2]), .clk(CLK), .clr(CLR));
  Register #(.width(1)) register_24 (
    .D(1'b1), .en(screenregsdec_1_out_24[2]), .Q(register_8_q[2]), .clk(CLK), .clr(CLR));
  Register #(.width(1)) register_25 (
    .D(1'b1), .en(screenregsdec_1_out_17[3]), .Q(register_1_q[3]), .clk(CLK), .clr(CLR));
  Register #(.width(1)) register_26 (
    .D(1'b1), .en(screenregsdec_1_out_18[3]), .Q(register_2_q[3]), .clk(CLK), .clr(CLR));
  Register #(.width(1)) register_27 (
    .D(1'b1), .en(screenregsdec_1_out_19[3]), .Q(register_3_q[3]), .clk(CLK), .clr(CLR));
  Register #(.width(1)) register_28 (
    .D(1'b1), .en(screenregsdec_1_out_20[3]), .Q(register_4_q[3]), .clk(CLK), .clr(CLR));
  Register #(.width(1)) register_29 (
    .D(1'b1), .en(screenregsdec_1_out_21[3]), .Q(register_5_q[3]), .clk(CLK), .clr(CLR));
  Register #(.width(1)) register_30 (
    .D(1'b1), .en(screenregsdec_1_out_22[3]), .Q(register_6_q[3]), .clk(CLK), .clr(CLR));
  Register #(.width(1)) register_31 (
    .D(1'b1), .en(screenregsdec_1_out_23[3]), .Q(register_7_q[3]), .clk(CLK), .clr(CLR));
  Register #(.width(1)) register_32 (
    .D(1'b1), .en(screenregsdec_1_out_24[3]), .Q(register_8_q[3]), .clk(CLK), .clr(CLR));
  Register #(.width(1)) register_33 (
    .D(1'b1), .en(screenregsdec_1_out_17[4]), .Q(register_1_q[4]), .clk(CLK), .clr(CLR));
  Register #(.width(1)) register_34 (
    .D(1'b1), .en(screenregsdec_1_out_18[4]), .Q(register_2_q[4]), .clk(CLK), .clr(CLR));
  Register #(.width(1)) register_35 (
    .D(1'b1), .en(screenregsdec_1_out_19[4]), .Q(register_3_q[4]), .clk(CLK), .clr(CLR));
  Register #(.width(1)) register_36 (
    .D(1'b1), .en(screenregsdec_1_out_20[4]), .Q(register_4_q[4]), .clk(CLK), .clr(CLR));
  Register #(.width(1)) register_37 (
    .D(1'b1), .en(screenregsdec_1_out_21[4]), .Q(register_5_q[4]), .clk(CLK), .clr(CLR));
  Register #(.width(1)) register_38 (
    .D(1'b1), .en(screenregsdec_1_out_22[4]), .Q(register_6_q[4]), .clk(CLK), .clr(CLR));
  Register #(.width(1)) register_39 (
    .D(1'b1), .en(screenregsdec_1_out_23[4]), .Q(register_7_q[4]), .clk(CLK), .clr(CLR));
  Register #(.width(1)) register_40 (
    .D(1'b1), .en(screenregsdec_1_out_24[4]), .Q(register_8_q[4]), .clk(CLK), .clr(CLR));
  Register #(.width(1)) register_41 (
    .D(1'b1), .en(screenregsdec_1_out_17[5]), .Q(register_1_q[5]), .clk(CLK), .clr(CLR));
  Register #(.width(1)) register_42 (
    .D(1'b1), .en(screenregsdec_1_out_17[6]), .Q(register_1_q[6]), .clk(CLK), .clr(CLR));
  Register #(.width(1)) register_43 (
    .D(1'b1), .en(screenregsdec_1_out_18[6]), .Q(register_2_q[6]), .clk(CLK), .clr(CLR));
  Register #(.width(1)) register_44 (
    .D(1'b1), .en(screenregsdec_1_out_18[5]), .Q(register_2_q[5]), .clk(CLK), .clr(CLR));
  Register #(.width(1)) register_45 (
    .D(1'b1), .en(screenregsdec_1_out_19[5]), .Q(register_3_q[5]), .clk(CLK), .clr(CLR));
  Register #(.width(1)) register_46 (
    .D(1'b1), .en(screenregsdec_1_out_19[6]), .Q(register_3_q[6]), .clk(CLK), .clr(CLR));
  Register #(.width(1)) register_47 (
    .D(1'b1), .en(screenregsdec_1_out_20[6]), .Q(register_4_q[6]), .clk(CLK), .clr(CLR));
  Register #(.width(1)) register_48 (
    .D(1'b1), .en(screenregsdec_1_out_20[5]), .Q(register_4_q[5]), .clk(CLK), .clr(CLR));
  Register #(.width(1)) register_49 (
    .D(1'b1), .en(screenregsdec_1_out_21[5]), .Q(register_5_q[5]), .clk(CLK), .clr(CLR));
  Register #(.width(1)) register_50 (
    .D(1'b1), .en(screenregsdec_1_out_21[6]), .Q(register_5_q[6]), .clk(CLK), .clr(CLR));
  Register #(.width(1)) register_51 (
    .D(1'b1), .en(screenregsdec_1_out_22[6]), .Q(register_6_q[6]), .clk(CLK), .clr(CLR));
  Register #(.width(1)) register_52 (
    .D(1'b1), .en(screenregsdec_1_out_22[5]), .Q(register_6_q[5]), .clk(CLK), .clr(CLR));
  Register #(.width(1)) register_53 (
    .D(1'b1), .en(screenregsdec_1_out_23[6]), .Q(register_7_q[6]), .clk(CLK), .clr(CLR));
  Register #(.width(1)) register_54 (
    .D(1'b1), .en(screenregsdec_1_out_23[5]), .Q(register_7_q[5]), .clk(CLK), .clr(CLR));
  Register #(.width(1)) register_55 (
    .D(1'b1), .en(screenregsdec_1_out_24[5]), .Q(register_8_q[5]), .clk(CLK), .clr(CLR));
  Register #(.width(1)) register_56 (
    .D(1'b1), .en(screenregsdec_1_out_24[6]), .Q(register_8_q[6]), .clk(CLK), .clr(CLR));
  Register #(.width(1)) register_57 (
    .D(1'b1), .en(screenregsdec_1_out_17[7]), .Q(register_1_q[7]), .clk(CLK), .clr(CLR));
  Register #(.width(1)) register_58 (
    .D(1'b1), .en(screenregsdec_1_out_18[7]), .Q(register_2_q[7]), .clk(CLK), .clr(CLR));
  Register #(.width(1)) register_59 (
    .D(1'b1), .en(screenregsdec_1_out_19[7]), .Q(register_3_q[7]), .clk(CLK), .clr(CLR));
  Register #(.width(1)) register_60 (
    .D(1'b1), .en(screenregsdec_1_out_20[7]), .Q(register_4_q[7]), .clk(CLK), .clr(CLR));
  Register #(.width(1)) register_61 (
    .D(1'b1), .en(screenregsdec_1_out_21[7]), .Q(register_5_q[7]), .clk(CLK), .clr(CLR));
  Register #(.width(1)) register_62 (
    .D(1'b1), .en(screenregsdec_1_out_22[7]), .Q(register_6_q[7]), .clk(CLK), .clr(CLR));
  Register #(.width(1)) register_63 (
    .D(1'b1), .en(screenregsdec_1_out_23[7]), .Q(register_7_q[7]), .clk(CLK), .clr(CLR));
  Register #(.width(1)) register_64 (
    .D(1'b1), .en(screenregsdec_1_out_24[7]), .Q(register_8_q[7]), .clk(CLK), .clr(CLR));
  Register register_65 (.D(register_1_q), .Q(out_6), .clk(FLASH));  // open: en, clr
  Register register_66 (.D(register_2_q), .Q(out_7), .clk(FLASH));  // open: en, clr
  Register register_67 (.D(register_3_q), .Q(out_8), .clk(FLASH));  // open: en, clr
  Register register_68 (.D(register_4_q), .Q(out_9), .clk(FLASH));  // open: en, clr
  Register register_69 (.D(register_5_q), .Q(out_10), .clk(FLASH));  // open: en, clr
  Register register_70 (.D(register_6_q), .Q(out_11), .clk(FLASH));  // open: en, clr
  Register register_71 (.D(register_7_q), .Q(out_12), .clk(FLASH));  // open: en, clr
  Register register_72 (.D(register_8_q), .Q(out_13), .clk(FLASH));  // open: en, clr
endmodule

module ScreenRegsDec (
  input  in_1,
  input  in_2,
  input  in_3,
  input  in_4,
  input  in_5,
  input  in_6,
  input  in_7,
  input  in_8,
  input  in_9,
  input  in_10,
  input  in_11,
  input  in_12,
  input  in_13,
  input  in_14,
  input  in_15,
  input  in_16,
  output [7:0] out_17,
  output [7:0] out_18,
  output [7:0] out_19,
  output [7:0] out_20,
  output [7:0] out_21,
  output [7:0] out_22,
  output [7:0] out_23,
  output [7:0] out_24
);

  and and_1 (out_17[0], in_9, in_1);
  and and_2 (out_18[0], in_10, in_1);
  and and_3 (out_19[0], in_11, in_1);
  and and_4 (out_20[0], in_12, in_1);
  and and_5 (out_21[0], in_13, in_1);
  and and_6 (out_22[0], in_14, in_1);
  and and_7 (out_23[0], in_15, in_1);
  and and_8 (out_24[0], in_16, in_1);
  and and_9 (out_17[1], in_9, in_2);
  and and_10 (out_18[1], in_10, in_2);
  and and_11 (out_19[1], in_11, in_2);
  and and_12 (out_20[1], in_12, in_2);
  and and_13 (out_21[1], in_13, in_2);
  and and_14 (out_22[1], in_14, in_2);
  and and_15 (out_23[1], in_15, in_2);
  and and_16 (out_24[1], in_16, in_2);
  and and_17 (out_17[2], in_9, in_3);
  and and_18 (out_18[2], in_10, in_3);
  and and_19 (out_19[2], in_11, in_3);
  and and_20 (out_20[2], in_12, in_3);
  and and_21 (out_21[2], in_13, in_3);
  and and_22 (out_22[2], in_14, in_3);
  and and_23 (out_23[2], in_15, in_3);
  and and_24 (out_24[2], in_16, in_3);
  and and_25 (out_17[3], in_9, in_4);
  and and_26 (out_18[3], in_10, in_4);
  and and_27 (out_19[3], in_11, in_4);
  and and_28 (out_20[3], in_12, in_4);
  and and_29 (out_21[3], in_13, in_4);
  and and_30 (out_22[3], in_14, in_4);
  and and_31 (out_23[3], in_15, in_4);
  and and_32 (out_24[3], in_16, in_4);
  and and_33 (out_17[4], in_9, in_5);
  and and_34 (out_18[4], in_10, in_5);
  and and_35 (out_19[4], in_11, in_5);
  and and_36 (out_20[4], in_12, in_5);
  and and_37 (out_21[4], in_13, in_5);
  and and_38 (out_22[4], in_14, in_5);
  and and_39 (out_23[4], in_15, in_5);
  and and_40 (out_24[4], in_16, in_5);
  and and_41 (out_17[5], in_9, in_6);
  and and_42 (out_18[5], in_10, in_6);
  and and_43 (out_19[5], in_11, in_6);
  and and_44 (out_20[5], in_12, in_6);
  and and_45 (out_21[5], in_13, in_6);
  and and_46 (out_22[5], in_14, in_6);
  and and_47 (out_23[5], in_15, in_6);
  and and_48 (out_24[5], in_16, in_6);
  and and_49 (out_17[6], in_9, in_7);
  and and_50 (out_18[6], in_10, in_7);
  and and_51 (out_19[6], in_11, in_7);
  and and_52 (out_20[6], in_12, in_7);
  and and_53 (out_21[6], in_13, in_7);
  and and_54 (out_22[6], in_14, in_7);
  and and_55 (out_23[6], in_15, in_7);
  and and_56 (out_24[6], in_16, in_7);
  and and_57 (out_17[7], in_9, in_8);
  and and_58 (out_18[7], in_10, in_8);
  and and_59 (out_19[7], in_11, in_8);
  and and_60 (out_20[7], in_12, in_8);
  and and_61 (out_21[7], in_13, in_8);
  and and_62 (out_22[7], in_14, in_8);
  and and_63 (out_23[7], in_15, in_8);
  and and_64 (out_24[7], in_16, in_8);
endmodule

module V2_0 (
);

  wire clock_1_out, clock_2_out, clock_3_out, not_1_out;
  wire [3:0] bit_extender_3_out;
  wire [7:0] alu_1_out_4, bit_extender_1_out, bit_extender_2_out, multiplexer_1_out, pc_1_out_4, ram_1_data,
       registergroupv3_1_out_7, registergroupv3_1_out_8, registergroupv3_1_out_9, registergroupv3_1_out_10,
       registergroupv3_1_out_11, screendecoder_1_out_6, screendecoder_1_out_7, screendecoder_1_out_8,
       screendecoder_1_out_9, screendecoder_1_out_10, screendecoder_1_out_11, screendecoder_1_out_12,
       screendecoder_1_out_13;
  wire [31:0] rom_1_data;

  Clock clock_1 (.out(clock_1_out));
  ROM #(.dataWidth(32)) rom_1 (.addr(pc_1_out_4), .data(rom_1_data));  // open: sel
  Bit_Extender #(.in_width(32), .out_width(8)) bit_extender_1 (.in(rom_1_data), .out(bit_extender_1_out));
  PC pc_1 (.CLK(clock_1_out), .out_4(pc_1_out_4), .Jump(rom_1_data[28]), .JumpPos(bit_extender_1_out));
  Clock clock_2 (.out(clock_2_out));
  Bit_Extender #(.in_width(10), .out_width(8)) bit_extender_2 (.in(rom_1_data[15:6]), .out(bit_extender_2_out));
  Bit_Extender #(.in_width(6), .out_width(4)) bit_extender_3 (.in(rom_1_data[5:0]), .out(bit_extender_3_out));
  RegisterGroupV3 registergroupv3_1 (
    .in_1(rom_1_data[25:21]), .in_2(rom_1_data[20:16]), .in_3(multiplexer_1_out), .in_4(rom_1_data[20:16]),
    .in_5(rom_1_data[31]), .in_6(clock_2_out), .out_7(registergroupv3_1_out_7),
    .out_8(registergroupv3_1_out_8), .out_9(registergroupv3_1_out_9), .out_10(registergroupv3_1_out_10),
    .out_11(registergroupv3_1_out_11));
  Multiplexer #(.width(8)) multiplexer_1 (
    .in0(alu_1_out_4), .in1(ram_1_data), .out(multiplexer_1_out), .sel(rom_1_data[30]));  // open: en
  ALU alu_1 (.in_1(bit_extender_3_out), .in_2(registergroupv3_1_out_7), .in_3(bit_extender_2_out), .out_4(alu_1_out_4));
  not not_1 (not_1_out, rom_1_data[29]);
  Clock clock_3 (.out(clock_3_out));
  ScreenDecoder screendecoder_1 (
    .Cols(registergroupv3_1_out_10), .Rows(registergroupv3_1_out_9), .CLK(registergroupv3_1_out_11[2]),
    .out_6(screendecoder_1_out_6), .out_7(screendecoder_1_out_7), .out_8(screendecoder_1_out_8),
    .out_9(screendecoder_1_out_9), .out_10(screendecoder_1_out_10), .out_11(screendecoder_1_out_11),
    .out_12(screendecoder_1_out_12), .out_13(screendecoder_1_out_13), .FLASH(registergroupv3_1_out_11[1]),
    .CLR(registergroupv3_1_out_11[0]));
  RAM #(.bus("separate")) ram_1 (
    .addr(alu_1_out_4), .din(registergroupv3_1_out_8), .data(ram_1_data), .str(rom_1_data[29]),
    .clk(clock_3_out), .ld(not_1_out));  // open: sel, clr
  DotMatrix #(.matrixcols(8), .matrixrows(8)) dotmatrix_1 (
    .col0(screendecoder_1_out_6), .col1(screendecoder_1_out_7), .col2(screendecoder_1_out_8),
    .col3(screendecoder_1_out_9), .col4(screendecoder_1_out_10), .col5(screendecoder_1_out_11),
    .col6(screendecoder_1_out_12), .col7(screendecoder_1_out_13));

  // Notes on the sheet:
  //   contents of rom_1 (hex, n*v repeats v):
  //   84e00046 84e10106 24010006 24010046 84e60046 c4040006 c4050046 84e60106 84e60086 c4010006 84210046
  //   24010006 84e60046 c4040006 c4050046 84e60106 84e60086
endmodule
