// Logisim project 第7-8话.circ as structural Verilog: 11 circuits, main circuit AU
module AU (
  input  in_1,
  input  [7:0] in_2,
  input  [7:0] in_3,
  output [7:0] out_4
);

  wire [7:0] adder_1_out, multiplexer_1_out, not_1_out;

  assign not_1_out = ~in_3;  // NOT_Gate not_1, 8 bits wide
  Adder adder_1 (.a(not_1_out), .b(8'h1), .out(adder_1_out));  // open: cin, cout
  Multiplexer #(.width(8)) multiplexer_1 (
    .in0(adder_1_out), .in1(in_3), .out(multiplexer_1_out), .sel(in_1));  // open: en
  Adder adder_2 (.a(in_2), .b(multiplexer_1_out), .out(out_4));  // open: cin, cout
endmodule

module LU (
  input  in_1,
  input  [7:0] in_2,
  input  [7:0] in_3,
  output [7:0] out_4
);

  wire [7:0] and_1_out, or_1_out;

  assign and_1_out = in_2 & in_3;  // AND_Gate and_1, 8 bits wide
  assign or_1_out = in_2 | in_3;  // OR_Gate or_1, 8 bits wide
  Multiplexer #(.width(8)) multiplexer_1 (.in0(or_1_out), .in1(and_1_out), .out(out_4), .sel(in_1));  // open: en
endmodule

module ALU (
  input  [3:0] in_1,
  input  [7:0] in_2,
  input  [7:0] in_3,
  output [7:0] out_4
);

  wire [7:0] au_1_out_4, lu_1_out_4;

  AU au_1 (.in_1(in_1[1]), .in_2(in_2), .in_3(in_3), .out_4(au_1_out_4));
  LU lu_1 (.in_1(in_1[0]), .in_2(in_2), .in_3(in_3), .out_4(lu_1_out_4));
  Multiplexer #(.width(8)) multiplexer_1 (.in0(lu_1_out_4), .in1(au_1_out_4), .out(out_4), .sel(in_1[2]));  // open: en
endmodule

module RegisterGroup (
  input  [4:0] in_1,
  input  [7:0] in_2,
  input  [4:0] in_3,
  input  in_4,
  input  in_5,
  output [7:0] out_6
);

  wire and_1_out, and_2_out, and_3_out, and_4_out, and_5_out, and_6_out, and_7_out, decoder_1_out0,
       decoder_1_out1, decoder_1_out2, decoder_1_out3, decoder_1_out4, decoder_1_out5, decoder_1_out6,
       decoder_1_out7;
  wire [7:0] register_1_q, register_2_q, register_3_q, register_4_q, register_5_q, register_6_q,
       register_7_q, register_8_q;

  Decoder #(.select(3)) decoder_1 (
    .out0(decoder_1_out0), .out1(decoder_1_out1), .out2(decoder_1_out2), .out3(decoder_1_out3),
    .out4(decoder_1_out4), .out5(decoder_1_out5), .out6(decoder_1_out6), .out7(decoder_1_out7),
    .sel(in_3[2:0]));  // open: en
  and and_1 (and_1_out, decoder_1_out0, in_4);
  and and_2 (and_2_out, decoder_1_out1, in_4);
  and and_3 (and_3_out, decoder_1_out2, in_4);
  and and_4 (and_4_out, decoder_1_out3, in_4);
  and and_5 (and_5_out, decoder_1_out4, in_4);
  and and_6 (and_6_out, decoder_1_out5, in_4);
  and and_7 (and_7_out, decoder_1_out6, in_4);
  // AND_Gate and_8 has open pins: in0=decoder_1_out7, in1=in_4, out=open
  Register register_1 (.D(in_2), .en(and_1_out), .Q(register_1_q), .clk(in_5));  // open: clr
  Register register_2 (.D(in_2), .en(and_2_out), .Q(register_2_q), .clk(in_5));  // open: clr
  Register register_3 (.D(in_2), .en(and_3_out), .Q(register_3_q), .clk(in_5));  // open: clr
  Register register_4 (.D(in_2), .en(and_4_out), .Q(register_4_q), .clk(in_5));  // open: clr
  Register register_5 (.D(in_2), .en(and_5_out), .Q(register_5_q), .clk(in_5));  // open: clr
  Register register_6 (.D(in_2), .en(and_6_out), .Q(register_6_q), .clk(in_5));  // open: clr
  Register register_7 (.D(in_2), .en(and_7_out), .Q(register_7_q), .clk(in_5));  // open: clr
  Register register_8 (.Q(register_8_q), .clr(1'b1));  // open: D, en, clk
  Multiplexer #(.select(3), .width(8)) multiplexer_1 (
    .in0(register_1_q), .in1(register_2_q), .in2(register_3_q), .in3(register_4_q), .in4(register_5_q),
    .in5(register_6_q), .in6(register_7_q), .in7(register_8_q), .out(out_6), .sel(in_1[2:0]));  // open: en
endmodule

module RegisterGroupV2 (
  input  [4:0] in_1,
  input  [4:0] in_2,
  input  [7:0] in_3,
  input  [4:0] in_4,
  input  in_5,
  input  in_6,
  output [7:0] out_7,
  output [7:0] out_8
);

  wire and_1_out, and_2_out, and_3_out, and_4_out, and_5_out, and_6_out, and_7_out, decoder_1_out0,
       decoder_1_out1, decoder_1_out2, decoder_1_out3, decoder_1_out4, decoder_1_out5, decoder_1_out6,
       decoder_1_out7;
  wire [2:0] bit_extender_1_out, bit_extender_2_out, bit_extender_3_out;
  wire [7:0] register_1_q, register_2_q, register_3_q, register_4_q, register_5_q, register_6_q,
       register_7_q, register_8_q;

  Bit_Extender #(.in_width(5), .out_width(3)) bit_extender_1 (.in(in_1), .out(bit_extender_1_out));
  Bit_Extender #(.in_width(5), .out_width(3)) bit_extender_2 (.in(in_2), .out(bit_extender_2_out));
  Decoder #(.select(3)) decoder_1 (
    .out0(decoder_1_out0), .out1(decoder_1_out1), .out2(decoder_1_out2), .out3(decoder_1_out3),
    .out4(decoder_1_out4), .out5(decoder_1_out5), .out6(decoder_1_out6), .out7(decoder_1_out7),
    .sel(bit_extender_3_out));  // open: en
  Bit_Extender #(.in_width(5), .out_width(3)) bit_extender_3 (.in(in_4), .out(bit_extender_3_out));
  and and_1 (and_1_out, decoder_1_out0, in_5);
  and and_2 (and_2_out, decoder_1_out1, in_5);
  and and_3 (and_3_out, decoder_1_out2, in_5);
  and and_4 (and_4_out, decoder_1_out3, in_5);
  and and_5 (and_5_out, decoder_1_out4, in_5);
  and and_6 (and_6_out, decoder_1_out5, in_5);
  and and_7 (and_7_out, decoder_1_out6, in_5);
  // AND_Gate and_8 has open pins: in0=decoder_1_out7, in1=in_5, out=open
  Register register_1 (.D(in_3), .en(and_1_out), .Q(register_1_q), .clk(in_6));  // open: clr
  Register register_2 (.D(in_3), .en(and_2_out), .Q(register_2_q), .clk(in_6));  // open: clr
  Register register_3 (.D(in_3), .en(and_3_out), .Q(register_3_q), .clk(in_6));  // open: clr
  Register register_4 (.D(in_3), .en(and_4_out), .Q(register_4_q), .clk(in_6));  // open: clr
  Register register_5 (.D(in_3), .en(and_5_out), .Q(register_5_q), .clk(in_6));  // open: clr
  Register register_6 (.D(in_3), .en(and_6_out), .Q(register_6_q), .clk(in_6));  // open: clr
  Register register_7 (.D(in_3), .en(and_7_out), .Q(register_7_q), .clk(in_6));  // open: clr
  Register register_8 (.Q(register_8_q), .clr(1'b1));  // open: D, en, clk
  Multiplexer #(.select(3), .width(8)) multiplexer_1 (
    .in0(register_1_q), .in1(register_2_q), .in2(register_3_q), .in3(register_4_q), .in4(register_5_q),
    .in5(register_6_q), .in6(register_7_q), .in7(register_8_q), .out(out_7), .sel(bit_extender_1_out));  // open: en
  Multiplexer #(.select(3), .width(8)) multiplexer_2 (
    .in0(register_1_q), .in1(register_2_q), .in2(register_3_q), .in3(register_4_q), .in4(register_5_q),
    .in5(register_6_q), .in6(register_7_q), .in7(register_8_q), .out(out_8), .sel(bit_extender_2_out));  // open: en
endmodule

module test (
  output [7:0] out_1,
  output [7:0] out_2
);

  wire clock_1_out, not_1_out;

  not not_1 (not_1_out, 1'b0);
  Clock clock_1 (.out(clock_1_out));
  ROM rom_1 (.addr(8'h1), .data(out_1));  // open: sel
  RAM #(.bus("separate")) ram_1 (
    .addr(8'h1), .din(8'h4), .data(out_2), .str(1'b0), .clk(clock_1_out), .ld(not_1_out));  // open: sel, clr
endmodule

module RGAndALU (
);

  wire clock_1_out, clock_2_out, not_1_out;
  wire [3:0] bit_extender_2_out;
  wire [7:0] alu_1_out_4, bit_extender_1_out, multiplexer_1_out, ram_1_data, registergroup_1_out_6, undriven;

  Clock clock_1 (.out(clock_1_out));
  Bit_Extender #(.in_width(10), .out_width(8)) bit_extender_1 (.in(10'h1), .out(bit_extender_1_out));
  Bit_Extender #(.in_width(6), .out_width(4)) bit_extender_2 (.in(6'b000100), .out(bit_extender_2_out));
  RegisterGroup registergroup_1 (
    .in_1({5{1'b0}}), .in_2(multiplexer_1_out), .in_3(5'b00001), .in_4(1'b1), .out_6(registergroup_1_out_6),
    .in_5(clock_1_out));
  Multiplexer #(.width(8)) multiplexer_1 (
    .in0(alu_1_out_4), .in1(ram_1_data), .out(multiplexer_1_out), .sel(1'b0));  // open: en
  ALU alu_1 (.in_1(bit_extender_2_out), .in_2(registergroup_1_out_6), .in_3(bit_extender_1_out), .out_4(alu_1_out_4));
  not not_1 (not_1_out, 1'b0);
  RAM #(.bus("separate")) ram_1 (
    .addr(undriven), .din(registergroup_1_out_6), .data(ram_1_data), .str(1'b0), .clk(clock_2_out),
    .ld(not_1_out));  // open: sel, clr
  Clock clock_2 (.out(clock_2_out));
endmodule

module CPU (
  input  [7:0] DRAMOut,
  input  [31:0] Ins,
  input  CLK,
  output [7:0] out_4,
  output W_R_prime,
  output [7:0] RAMAddr,
  output [7:0] RAMIn
);

  wire [3:0] bit_extender_2_out;
  wire [7:0] bit_extender_1_out, multiplexer_1_out, registergroupv2_1_out_7;

  PC pc_1 (.in_1(CLK), .out_2(out_4));
  RegisterGroupV2 registergroupv2_1 (
    .in_1(Ins[25:21]), .in_2(Ins[20:16]), .in_3(multiplexer_1_out), .in_4(Ins[20:16]), .in_5(Ins[31]),
    .in_6(CLK), .out_7(registergroupv2_1_out_7), .out_8(RAMIn));
  Bit_Extender #(.in_width(10), .out_width(8)) bit_extender_1 (.in(Ins[15:6]), .out(bit_extender_1_out));
  Bit_Extender #(.in_width(6), .out_width(4)) bit_extender_2 (.in(Ins[5:0]), .out(bit_extender_2_out));
  Multiplexer #(.width(8)) multiplexer_1 (
    .in0(RAMAddr), .in1(DRAMOut), .out(multiplexer_1_out), .sel(Ins[30]));  // open: en
  ALU alu_1 (.in_1(bit_extender_2_out), .in_2(registergroupv2_1_out_7), .in_3(bit_extender_1_out), .out_4(RAMAddr));

  assign W_R_prime = Ins[29];
endmodule

module Motherboard (
);

  wire clock_1_out, cpu_1_w_r_prime, not_1_out;
  wire [7:0] cpu_1_out_4, cpu_1_ramaddr, cpu_1_ramin, ram_1_data;
  wire [31:0] rom_1_data;

  ROM #(.dataWidth(32)) rom_1 (.addr(cpu_1_out_4), .data(rom_1_data));  // open: sel
  Clock clock_1 (.out(clock_1_out));
  CPU cpu_1 (
    .Ins(rom_1_data), .W_R_prime(cpu_1_w_r_prime), .RAMIn(cpu_1_ramin), .RAMAddr(cpu_1_ramaddr),
    .CLK(clock_1_out), .DRAMOut(ram_1_data), .out_4(cpu_1_out_4));
  RAM #(.bus("separate")) ram_1 (
    .addr(cpu_1_ramaddr), .din(cpu_1_ramin), .data(ram_1_data), .str(cpu_1_w_r_prime), .clk(clock_1_out),
    .ld(not_1_out));  // open: sel, clr
  not not_1 (not_1_out, cpu_1_w_r_prime);

  // Notes on the sheet:
  //   contents of rom_1 (hex, n*v repeats v):
  //   80e00046 80e10106 20010006 20010046 c0010006 80210046 20010006
endmodule

module PC (
  input  in_1,
  output [7:0] out_2
);

  wire [7:0] adder_1_out;

  Register register_1 (.D(adder_1_out), .Q(out_2), .clk(in_1));  // open: en, clr
  Adder adder_1 (.a(out_2), .b(8'h1), .out(adder_1_out));  // open: cin, cout
endmodule

module V1_1 (
);

  wire clock_1_out, clock_2_out, clock_3_out, not_1_out;
  wire [3:0] bit_extender_2_out;
  wire [7:0] alu_1_out_4, bit_extender_1_out, multiplexer_1_out, pc_1_out_2, ram_1_data,
       registergroupv2_1_out_7, registergroupv2_1_out_8;
  wire [31:0] rom_1_data;

  Clock clock_1 (.out(clock_1_out));
  ROM #(.dataWidth(32)) rom_1 (.addr(pc_1_out_2), .data(rom_1_data));  // open: sel
  PC pc_1 (.in_1(clock_1_out), .out_2(pc_1_out_2));
  Bit_Extender #(.in_width(10), .out_width(8)) bit_extender_1 (.in(rom_1_data[15:6]), .out(bit_extender_1_out));
  Bit_Extender #(.in_width(6), .out_width(4)) bit_extender_2 (.in(rom_1_data[5:0]), .out(bit_extender_2_out));
  RegisterGroupV2 registergroupv2_1 (
    .in_1(rom_1_data[25:21]), .in_2(rom_1_data[20:16]), .in_3(multiplexer_1_out), .in_4(rom_1_data[20:16]),
    .in_5(rom_1_data[31]), .in_6(clock_2_out), .out_7(registergroupv2_1_out_7),
    .out_8(registergroupv2_1_out_8));
  Clock clock_2 (.out(clock_2_out));
  Multiplexer #(.width(8)) multiplexer_1 (
    .in0(alu_1_out_4), .in1(ram_1_data), .out(multiplexer_1_out), .sel(rom_1_data[30]));  // open: en
  ALU alu_1 (.in_1(bit_extender_2_out), .in_2(registergroupv2_1_out_7), .in_3(bit_extender_1_out), .out_4(alu_1_out_4));
  not not_1 (not_1_out, rom_1_data[29]);
  Clock clock_3 (.out(clock_3_out));
  RAM #(.bus("separate")) ram_1 (
    .addr(alu_1_out_4), .din(registergroupv2_1_out_8), .data(ram_1_data), .str(rom_1_data[29]),
    .clk(clock_3_out), .ld(not_1_out));  // open: sel, clr
endmodule
